# Fritzing sketch CanSat_PCB_Source (saved by Fritzing 1.0.6)
circuit board: 8.8cm x 8.8cm

parts:
  MCU_#1 = ESP-WROOM-32 [ESP-32S] Module [part_number=ESP-WROOM-32]
  MCU_#2 = ESP-WROOM-32 [ESP-32S] Module [part_number=ESP-WROOM-32]
  Battery_Connector = JST XH_2.54mm Horizontal SMD_Connector 2pin [package=SMD]
  5V_Regulator = Voltage Regulator [package=7805-upright]
  Power_Switch = Toggle Switch [package=THT]
  Servo_Header_#1 = Header 3 [package=1x03-1mm-ra]
  3V3_Regulator = MPC1700 [package=sot23-3]
  Resistor_#1 = Resistor [tolerance=±5% power=0.25W resistance=10k package=THT]
  Upload_#1 = Momentary Switch [package=tactile-pth]
  Reset_#1 = Momentary Switch [package=tactile-pth]
  Reset_#2 = Momentary Switch [package=tactile-pth]
  Upload_#2 = Momentary Switch [package=tactile-pth]
  Servo_Header_#2 = Header 3 [package=1x03-1mm-ra]
  Programming_Headers_#1 = Header 6 [package=em406]
  Programming_Headers_#2 = Header 6 [package=em406]
  BMP280_#2 = Adafruit BMP280 [part_number="Adafruit #2651"]
  MPU_#2 = Adafruit MPU6050
  BMP280_#1 = Adafruit BMP280 [part_number="Adafruit #2651"]
  MPU_#1 = Adafruit MPU6050
  Capacitor_#1 = Electrolytic Capacitor [capacitance=1µF voltage=35V package="100 mil [THT, electrolytic]"]
  Capacitor_#2 = Electrolytic Capacitor [capacitance=1µF voltage=35V package="100 mil [THT, electrolytic]"]
  Resistor_#2 = Resistor [tolerance=±5% power=0.25W resistance=10k package=THT]

nets:
  GND: MCU_#1.GND#0, BMP280_#1.GND, BMP280_#1.SDO/ADR, MPU_#1.GND, MPU_#1.AD0
  3.3V: MCU_#1.3V3, MCU_#2.3V3, MCU_#2.IO22, 3V3_Regulator.OUT, Resistor_#1.Pin_0, Programming_Headers_#1.1, Programming_Headers_#2.1, BMP280_#2.SCK/SCL, BMP280_#2.3.3V, BMP280_#2.CS, MPU_#2.SCL, MPU_#2.3.3V, BMP280_#1.3.3V, BMP280_#1.CS, MPU_#1.3.3V, Resistor_#2.Pin_0
  N1: MCU_#1.EN, Resistor_#1.Pin_1, Reset_#1.3, Programming_Headers_#1.5, Capacitor_#1.+
  N2: MCU_#1.IO13, Servo_Header_#1.3
  N3: MCU_#1.GND#51, Programming_Headers_#1.2
  N4: MCU_#1.IO0, Upload_#1.1, Programming_Headers_#1.6
  N5: MCU_#1.IO21, BMP280_#1.SDI/SDA, MPU_#1.SDA
  N6: MCU_#1.RXD0, Programming_Headers_#1.4
  N7: MCU_#1.TXD0, Programming_Headers_#1.3
  N8: MCU_#1.IO22, BMP280_#1.SCK/SCL, MPU_#1.SCL
  GND_2: MCU_#1.RST, MCU_#2.RST, Battery_Connector.pin2, 5V_Regulator.GND, Servo_Header_#1.2, 3V3_Regulator.GND, Upload_#1.3, Reset_#1.1, Upload_#2.3, Servo_Header_#2.2, Capacitor_#1.-
  GND_3: MCU_#2.GND#0, BMP280_#2.GND, BMP280_#2.SDO/ADR, MPU_#2.GND, MPU_#2.AD0
  N9: MCU_#2.EN, Reset_#2.3, Programming_Headers_#2.5, Capacitor_#2.+, Resistor_#2.Pin_1
  N10: MCU_#2.IO13, Servo_Header_#2.3
  N11: MCU_#2.GND#50, Reset_#2.1, Capacitor_#2.-
  N12: MCU_#2.GND#51, Programming_Headers_#2.2
  N13: MCU_#2.IO0, Upload_#2.1, Programming_Headers_#2.6
  N14: MCU_#2.IO21, BMP280_#2.SDI/SDA, MPU_#2.SDA
  N15: MCU_#2.RXD0, Programming_Headers_#2.4
  N16: MCU_#2.TXD0, Programming_Headers_#2.3
  N17: Battery_Connector.pin1, Power_Switch.L1
  N18: 5V_Regulator.IN, Power_Switch.COM, 3V3_Regulator.IN
  N19: 5V_Regulator.OUT, Servo_Header_#1.1, Servo_Header_#2.1

custom parts:
  ESP-WROOM-32 [ESP-32S] Module: Espressif ESP-WROOM-32 WiFi/Bluetooth LE microcontroller module also known as the Ai-Thinker ESP-32S module with similar formfactor. The ESP32 is a microcontroller chip with WiFi and BLE capabilities. The chip is developed by Espressif and is the successor to the popular ESP8266 WiFi module.
  JST XH_2.54mm Horizontal SMD_Connector 2pin: JST XH_2.54mm Horizontal SMD_Connector 2pin.
  Voltage Regulator: Voltage Regulator Standard 7805 5V regulator. IGO (Input Ground Output). Spark Fun Electronics SKU : COM-00107
  MPC1700: Small package LDO
  Adafruit BMP280: Bosch has stepped up their game with their new BMP280 sensor, an environmental sensor with temperature, barometric pressure that is the next generation upgrade to the BMP085/BMP180/BMP183. This sensor is great for all sorts of weather sensing and can even be used in both I2C and SPI! This precision sensor from Bosch is the best low-cost, precision sensing solution for measuring barometric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
  Adafruit MPU6050: The MPU-6050 is a popular six axis accelerometer and gyroscope (gyro) that has all the info you need on how things are shakin' and spinnin' . With six axes of sensing and 16-bit measurements, you'll have everything you need to give your robot friend an inner ear. This combination of gyroscopes and accelerometers is commonly referred to as an Inertial Measurement Unit or IMU. Not so long ago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
